# Fritzing sketch Phoniebox (saved by Fritzing 1.0.4)

parts:
  MCU1 = Raspberry Pi Zero
  onoffshim1 = Pimoroni OnOffShim  # not connected
  Bauteil1 = RFID-RC522-v2
  onoffshim2 = Pimoroni OnOffShim  # not connected

nets:
  N1: MCU1.pin_17, Bauteil1.3.3V
  N2: MCU1.pin_19, Bauteil1.MOSI
  N3: MCU1.pin_21, Bauteil1.MISO
  N4: MCU1.pin_22, Bauteil1.RST
  N5: MCU1.pin_23, Bauteil1.SCK
  N6: MCU1.pin_24, Bauteil1.SDA
  N7: MCU1.pin_25, MCU1.pin_34, Bauteil1.GND

custom parts:
  RFID-RC522-v2: A simple China made RFID-RC522 Reader; do check the pin labels, as this is a MFRC522 based clone.
